# Fritzing sketch USBtinyISP-ATtiny85 (saved by Fritzing 0.7.4b)
breadboards: 1

parts:
  U1 = attiny85 [package=dip]
  USBtinyISP1 = Generic shrouded header - 6 pins [form="♂ (shrouded male)" package=THT]

nets:
  N1: U1.Pin_1, USBtinyISP1.Reset
  N2: U1.Pin_4, USBtinyISP1.Ground
  N3: U1.Pin_5, USBtinyISP1.MOSI
  N4: U1.Pin_6, USBtinyISP1.MISO
  N5: U1.Pin_7, USBtinyISP1.SCK
  N6: U1.Pin_8, USBtinyISP1.+Vss

custom parts:
  Generic shrouded header - 6 pins: Generic shrouded header
