# Fritzing sketch ATtiny85-LED-Button (saved by Fritzing 0.7.4b)
breadboards: 1

parts:
  U1 = attiny85 [package=dip]
  S1 = Pushbutton [package="[SMD]"]
  LED1 = LED - 5mm [color="Red (633nm)" package="5 mm [THT]"]

nets:
  N1: U1.Pin_2, S1.Pin_3, S1.Pin_4
  N2: U1.Pin_3, LED1.anode
  GND: U1.Pin_4, LED1.cathode
  N3: U1.Pin_8, S1.Pin_1, S1.Pin_2

notes:
  Power line here
  Ground line here
